# Fritzing sketch Teste ADS1220 (saved by Fritzing 0.9.5d)
breadboards: 1

parts:
  M1 = DOIT Esp32 DevKit v1 (30 pins long, 11 pins width) [part_number=ESP32S-PIN30]
  microSD1 = MicroSD Card Module
  ZS-042_RTC1 = ZS-042 RTC Module
  A1 = CJMCU-1220 module

nets:
  VCC: M1.3V3, microSD1.VCC, ZS-042_RTC1.VCC
  N1: M1.D21, ZS-042_RTC1.SDA
  GND: M1.GND, microSD1.GND, ZS-042_RTC1.GND
  N2: microSD1.MISO, A1.Pin_1, A1.Pin_2
  N3: microSD1.MOSI, A1.Pin_3

notes:
  Pino do DS3231
  Pino do ESP32
  VCC
  3V3
  GND
  GND
  SDA
  GPIO 21
  SCL
  GPIO 22

custom parts:
  DOIT Esp32 DevKit v1 (30 pins long, 11 pins width): The DOIT Esp32 DevKit v1 is one of the development board created by DOIT to evaluate the ESP-WROOM-32 module. It is based on the ESP32 microcontroller that boasts Wifi, Bluetooth, Ethernet and Low Power support all in a single chip. (vanepp) made breadboard work, adjusted pin numbering and labels and reduced size of schematic and cleaned up pcb. This chip is 30pins long (2 x15) and 11 pins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
  CJMCU-1220 module: The ADS1220 is a precision 24-bit analog-to-digital converter (ADC) that provides many integrated features to reduce system cost and component count for small sensor signals.
